# Fritzing sketch Knapper (saved by Fritzing 0.7.10b)
breadboards: 1

parts:
  S1 = Pushbutton [package=THT]
  S2 = Pushbutton [package=THT]
  S3 = Pushbutton [package=THT]
  J1 = female pin header, 2 pins [form="♀ (female)"]
  J2 = female pin header, 2 pins [form="♀ (female)"]
  J3 = female pin header, 2 pins [form="♀ (female)"]  # not connected
  J4 = female pin header, 2 pins [form="♀ (female)"]  # not connected

nets:
  N1: S1.leg0, S2.leg0, S3.leg0, J2.pin1
  N2: S1.leg1, J1.pin2
  N3: S2.leg1, J1.pin1
  N4: S3.leg1, J2.pin2
